// Logisim project NAND2Tetris_logisim.circ as structural Verilog: 8 circuits, main circuit main
module main (
);
endmodule

module Mux4Way16 (
  input  [15:0] a16,
  input  [15:0] b16,
  input  [15:0] c16,
  input  [15:0] d16,
  input  [1:0] sel2,
  output [15:0] out16
);

  wire [15:0] multiplexer_1_out, multiplexer_2_out;

  Multiplexer #(.width(16), .enable("false")) multiplexer_1 (
    .in0(a16), .in1(b16), .out(multiplexer_1_out), .sel(sel2[0]));
  Multiplexer #(.width(16), .enable("false")) multiplexer_2 (
    .in0(c16), .in1(d16), .out(multiplexer_2_out), .sel(sel2[0]));
  Multiplexer #(.width(16), .enable("false")) multiplexer_3 (
    .in0(multiplexer_1_out), .in1(multiplexer_2_out), .out(out16), .sel(sel2[1]));
endmodule

module Mux8Way16 (
  input  [15:0] a16,
  input  [15:0] b16,
  input  [15:0] c16,
  input  [15:0] d16,
  input  [15:0] e16,
  input  [15:0] f16,
  input  [15:0] g16,
  input  [15:0] h16,
  input  [2:0] sel3,
  output [15:0] out16
);

  wire [15:0] mux4way16_1_out16, mux4way16_2_out16;

  Mux4Way16 mux4way16_1 (.a16(a16), .b16(b16), .c16(c16), .d16(d16), .sel2(sel3[1:0]), .out16(mux4way16_1_out16));
  Mux4Way16 mux4way16_2 (.a16(e16), .b16(f16), .c16(g16), .d16(h16), .sel2(sel3[1:0]), .out16(mux4way16_2_out16));
  Multiplexer #(.width(16), .enable("false")) multiplexer_1 (
    .in0(mux4way16_1_out16), .in1(mux4way16_2_out16), .out(out16), .sel(sel3[2]));
endmodule

module Or8Way (
  input  [7:0] in8,
  output out1
);

  wire or_1_out, or_2_out, or_3_out, or_4_out, or_5_out, or_6_out;

  or or_1 (or_1_out, in8[0], in8[1]);
  or or_2 (or_2_out, in8[2], in8[3]);
  or or_3 (or_3_out, in8[4], in8[5]);
  or or_4 (or_4_out, in8[6], in8[7]);
  or or_5 (or_5_out, or_1_out, or_2_out);
  or or_6 (or_6_out, or_3_out, or_4_out);
  or or_7 (out1, or_5_out, or_6_out);
endmodule

module DMux4Way (
  input  in1,
  input  [1:0] sel2,
  output a1,
  output b1,
  output c1,
  output d1
);

  wire demultiplexer_1_out0, demultiplexer_1_out1;

  Demultiplexer #(.enable("false")) demultiplexer_1 (
    .out0(demultiplexer_1_out0), .out1(demultiplexer_1_out1), .in(in1), .sel(sel2[1]));
  Demultiplexer #(.enable("false")) demultiplexer_2 (.out0(a1), .out1(b1), .in(demultiplexer_1_out0), .sel(sel2[0]));
  Demultiplexer #(.enable("false")) demultiplexer_3 (.out0(c1), .out1(d1), .in(demultiplexer_1_out1), .sel(sel2[0]));
endmodule

module DMux8Way (
  input  in1,
  input  [2:0] sel3,
  output a1,
  output b1,
  output c1,
  output d1,
  output e1,
  output f1,
  output g1,
  output h1
);

  wire demultiplexer_1_out0, demultiplexer_1_out1;

  Demultiplexer #(.enable("false")) demultiplexer_1 (
    .out0(demultiplexer_1_out0), .out1(demultiplexer_1_out1), .in(in1), .sel(sel3[2]));
  DMux4Way dmux4way_1 (.in1(demultiplexer_1_out0), .sel2(sel3[1:0]), .a1(a1), .b1(b1), .c1(c1), .d1(d1));
  DMux4Way dmux4way_2 (.in1(demultiplexer_1_out1), .sel2(sel3[1:0]), .a1(e1), .b1(f1), .c1(g1), .d1(h1));
endmodule

module HalfAdder (
  input  a,
  input  b,
  output sum,
  output carry
);

  xor xor_1 (sum, a, b);
  and and_1 (carry, a, b);
endmodule

// janisims
module FullAdderN2ndcell (
  input  a,
  input  b,
  input  c,
  output sum,
  output carry
);

  wire halfadder_1_carry, halfadder_1_sum, halfadder_2_carry;

  HalfAdder halfadder_1 (.a(a), .b(b), .sum(halfadder_1_sum), .carry(halfadder_1_carry));
  HalfAdder halfadder_2 (.a(halfadder_1_sum), .b(c), .sum(sum), .carry(halfadder_2_carry));
  xor xor_1 (carry, halfadder_2_carry, halfadder_1_carry);
endmodule
